// Logisim project MIPS-logisim.circ as structural Verilog: 21 circuits, main circuit main
module main (
  input  in_1,
  input  in_2,
  input  in_3,
  input  in_4,
  output [31:0] out_5,
  output [31:0] out_6,
  output [31:0] out_7,
  output [31:0] out_8,
  output [31:0] out_9,
  output out_10
);

  wire alu_1_out_overflow, and_1_out, and_2_out, and_3_out, and_7_out, and_8_out, and_9_out, and_11_out,
       and_12_out, and_13_out, and_14_out, and_15_out, and_16_out, clk_brp, clr_pc, comparator_1_eq,
       comparator_2_eq, comparator_3_eq, comparator_4_eq, comparator_4_gt, comparator_4_lt, comparator_5_eq,
       comparator_6_eq, comparator_7_eq, comparator_8_eq, Ex_Mem2Reg, Ex_MemWr, Ex_RegWr, Ex_Sel, FlushID2,
       FlushID22, fwID_flgJump, fwMem_RegWr, fwWB_RegWr, ID_ALUimm, ID_Branch, ID_ExtOp, ID_Mem2Reg,
       ID_MemWr, ID_Mov, ID_MovAcc, ID_RegWr, ID_Sel, inEx_Branch, inEx_Mov, inEx_MovAcc, inID_Branch,
       inID_Jump, inMem_Sel, Mem_Mem2Reg, mips_decoder_1_memwr, mips_decoder_1_regwr, multiplexer_7_out,
       n_FlushEX, n_FlushID, n_stall_EX, n_stall_ID, n_stall_IF, n_stall_MEM, n_stall_WB, nor5_1_wire_out,
       nor5_2_wire_out, not_1_out, not_2_out, not_3_out, or_1_out, or_2_out, or_4_out, or_9_out, or_10_out,
       RegDst, register_2_q, register_16_q, register_17_q, register_19_q, register_20_q, register_27_q,
       Rtype, stall_EX_MDU, stall_ID, Working, xnor_1_out, xnor_2_out;
  wire [1:0] Ex_AAOp, ID_AAOp, inMem_AAOp;
  wire [2:0] inID_BranchOp;
  wire [3:0] bit_extender_1_out, ID_MDUop, mips_decoder_1_mduop;
  wire [3:1] Ex_WEMask;
  wire [4:0] Ex_Rw, fwMem_Rw, fwWB_Rw, ID_ALUctl, ID_Rw, multiplexer_11_out, register_15_q, register_21_q;
  wire [5:0] func;
  wire [7:0] bit_extender_2_out, bit_extender_4_out, bit_extender_6_out;
  wire [15:0] bit_extender_5_out, register_14_q;
  wire [15:6] ID_imm16;
  wire [25:16] inID_jtarget;
  wire [29:0] adder_2_out, bit_extender_3_out, fwID_jtarget, ID_nextpc, IF_nextpc, multiplexer_1_out,
       multiplexer_3_out, multiplexer_16_out, PC_q, register_11_q;
  wire [31:0] alu_1_out_result, and_19_out, bit_extender_7_out, DRAMout, Ex_ALUout, Ex_BusB,
       ext_mux8_1_out_32, ext_mux16_1_out_32, ext_mux16_2_out_32, fwMem_data, fwWB_data, ID_BusA, ID_BusB,
       inEx_Acc, inEx_Hi, inEx_Lo, inID_DataA, inID_DataB, Mem_ALUout, Mem_BusW, multiplexer_2_out,
       multiplexer_4_out, multiplexer_5_out, multiplexer_9_out, multiplexer_10_out, multiplexer_14_out,
       multiplexer_15_out, multiplexer_21_out, multiplexer_22_out, multiplexer_23_out, multiplexer_24_out,
       ram_1_dout, register_4_q, register_12_q, register_25_q, register_26_q;
  wire [31:26] instr;

  Multiplexer #(.width(30)) multiplexer_1 (
    .in0(multiplexer_3_out), .in1({30{1'b0}}), .out(multiplexer_1_out), .sel(clr_pc));
  Register #(.trigger("falling"), .width(1)) register_1 (.D(1'b1), .en(1'b1), .clk(clk_brp), .Q(Working), .clr(in_3));
  Register #(.trigger("falling"), .width(30)) PC (
    .D(multiplexer_1_out), .en(n_stall_IF), .clk(clk_brp), .Q(PC_q));  // open: clr
  Register #(.trigger("falling"), .width(1)) register_2 (
    .D(stall_ID), .clk(clk_brp), .Q(register_2_q), .clr(in_3));  // open: en
  and and_1 (and_1_out, stall_ID, not_1_out);
  not not_1 (not_1_out, register_2_q);
  Comparator #(.mode("unsigned"), .width(5)) comparator_1 (
    .a(inID_jtarget[25:21]), .b(fwWB_Rw), .eq(comparator_1_eq));  // open: gt, lt
  Comparator #(.mode("unsigned"), .width(5)) comparator_2 (
    .a(inID_jtarget[20:16]), .b(fwWB_Rw), .eq(comparator_2_eq));  // open: gt, lt
  Comparator #(.mode("unsigned"), .width(32)) comparator_3 (
    .a({32{1'b0}}), .b(ID_BusB), .eq(comparator_3_eq));  // open: gt, lt
  Multiplexer #(.width(32)) multiplexer_2 (.in0({32{1'b0}}), .in1(ID_BusB), .out(multiplexer_2_out), .sel(xnor_1_out));
  NotExactlyOne xnor_1 (.out(xnor_1_out), .in0(inID_BranchOp[2]), .in1(inID_BranchOp[1]), .in2(inID_BranchOp[0]));
  Adder #(.width(30)) adder_1 (.a(PC_q), .b(30'h1), .out(IF_nextpc));  // open: cin, cout
  Register #(.trigger("falling"), .width(30)) register_3 (
    .D(IF_nextpc), .en(n_stall_ID), .clk(clk_brp), .Q(ID_nextpc));  // open: clr
  Register #(.trigger("falling"), .width(32)) register_4 (
    .D(out_5), .en(and_1_out), .clk(clk_brp), .Q(register_4_q), .clr(in_3));
  mips_decoder mips_decoder_1 (
    .in_Rt(inID_jtarget[20:16]), .in_op(instr), .in_func(func), .Rtype(Rtype), .RegWr(mips_decoder_1_regwr),
    .RegDst(RegDst), .Sel(ID_Sel), .ALUsrc(ID_ALUimm), .MemtoReg(ID_Mem2Reg), .MemWr(mips_decoder_1_memwr),
    .Branch(inID_Branch), .Jump(inID_Jump), .EXTctr(ID_ExtOp), .AAop(ID_AAOp), .BranchOp(inID_BranchOp),
    .ALUctl(ID_ALUctl), .Mov(ID_Mov), .MovAcc(ID_MovAcc), .MDUop(mips_decoder_1_mduop));
  and and_2 (and_2_out, comparator_1_eq, fwWB_RegWr);
  and and_3 (and_3_out, comparator_2_eq, fwWB_RegWr);
  Comparator #(.mode("unsigned"), .width(32)) comparator_4 (
    .a(ID_BusA), .b(multiplexer_2_out), .gt(comparator_4_gt), .eq(comparator_4_eq), .lt(comparator_4_lt));
  Register #(.trigger("falling"), .width(32)) register_5 (
    .D(Ex_ALUout), .clk(clk_brp), .Q(Mem_ALUout));  // open: en, clr
  Register #(.trigger("falling"), .width(1)) register_6 (
    .D(Ex_Mem2Reg), .clk(clk_brp), .Q(Mem_Mem2Reg));  // open: en, clr
  Register #(.trigger("falling"), .width(5)) register_7 (.D(Ex_Rw), .clk(clk_brp), .Q(fwMem_Rw));  // open: en, clr
  Register #(.trigger("falling"), .width(1)) register_8 (
    .D(Ex_RegWr), .clk(clk_brp), .Q(fwMem_RegWr));  // open: en, clr
  Register #(.trigger("falling"), .width(2)) register_9 (.D(Ex_AAOp), .clk(clk_brp), .Q(inMem_AAOp));  // open: en, clr
  Register #(.trigger("falling"), .width(1)) register_10 (.D(Ex_Sel), .clk(clk_brp), .Q(inMem_Sel));  // open: en, clr
  Multiplexer #(.width(30)) multiplexer_3 (
    .in0(IF_nextpc), .in1(fwID_jtarget), .out(multiplexer_3_out), .sel(fwID_flgJump));
  Multiplexer #(.width(32)) multiplexer_4 (.in0(inID_DataA), .in1(fwWB_data), .out(multiplexer_4_out), .sel(and_2_out));
  Multiplexer #(.width(32)) multiplexer_5 (.in0(inID_DataB), .in1(fwWB_data), .out(multiplexer_5_out), .sel(and_3_out));
  xnor xnor_2 (xnor_2_out, comparator_3_eq, ID_Sel);
  Multiplexer #(.width(32)) multiplexer_6 (
    .in0(out_5), .in1(register_4_q), .out({instr, inID_jtarget, ID_imm16, func}), .sel(register_2_q));
  assign bit_extender_1_out = {{3{n_FlushID}}, n_FlushID};  // Bit_Extender bit_extender_1
  reg32 reg32_1 (
    .clear(in_3), .in_Ra(inID_jtarget[25:21]), .in_Rb(inID_jtarget[20:16]), .in_Rw(fwWB_Rw),
    .in_WE(fwWB_RegWr), .in_Rwdata(fwWB_data), .clk(clk_brp), .out_Ra(inID_DataA), .out_Rb(inID_DataB));
  and and_4 (FlushID22, xnor_2_out, ID_Mov);
  or or_1 (or_1_out, comparator_4_eq, comparator_4_gt);
  or or_2 (or_2_out, comparator_4_lt, comparator_4_eq);
  not not_2 (not_2_out, comparator_4_eq);
  assign ID_MDUop = mips_decoder_1_mduop & bit_extender_1_out;  // AND_Gate and_5, 4 bits wide
  Comparator #(.mode("unsigned"), .width(5)) comparator_5 (
    .a(inID_jtarget[25:21]), .b(fwMem_Rw), .eq(comparator_5_eq));  // open: gt, lt
  Comparator #(.mode("unsigned"), .width(5)) comparator_6 (
    .a(fwMem_Rw), .b(inID_jtarget[20:16]), .eq(comparator_6_eq));  // open: gt, lt
  Multiplexer #(.select(3)) multiplexer_7 (
    .in0(comparator_4_eq), .in1(or_1_out), .in2(or_1_out), .in3(comparator_4_gt), .in4(or_2_out),
    .in5(comparator_4_lt), .in6(comparator_4_lt), .in7(not_2_out), .out(multiplexer_7_out),
    .sel(inID_BranchOp));
  Bit_Extender #(.in_width(30), .out_width(8)) bit_extender_2 (.in(PC_q), .out(bit_extender_2_out));
  and and_6 (ID_RegWr, mips_decoder_1_regwr, n_FlushID);
  Multiplexer #(.width(32)) multiplexer_8 (.in0(Mem_ALUout), .in1(Mem_BusW), .out(fwMem_data), .sel(Mem_Mem2Reg));
  RAM #(.dataWidth(32), .trigger("falling")) ram_1 (
    .addr(bit_extender_2_out), .oe(1'b1), .clk(clk_brp), .dout(ram_1_dout));  // open: we, din
  Multiplexer #(.width(32)) multiplexer_9 (
    .in0(multiplexer_4_out), .in1(fwMem_data), .out(multiplexer_9_out), .sel(and_7_out));
  and and_7 (and_7_out, comparator_5_eq, fwMem_RegWr);
  and and_8 (and_8_out, fwMem_RegWr, comparator_6_eq);
  Multiplexer #(.width(32)) multiplexer_10 (
    .in0(multiplexer_5_out), .in1(fwMem_data), .out(multiplexer_10_out), .sel(and_8_out));
  or or_3 (fwID_flgJump, inID_Jump, and_9_out);
  and and_9 (and_9_out, multiplexer_7_out, inID_Branch);
  Multiplexer #(.width(5)) multiplexer_11 (
    .in0(inID_jtarget[20:16]), .in1(ID_imm16[15:11]), .out(multiplexer_11_out), .sel(RegDst));
  and and_10 (ID_MemWr, mips_decoder_1_memwr, n_FlushID);
  or or_4 (or_4_out, and_11_out, and_12_out);
  and and_11 (and_11_out, inID_Branch, ID_RegWr);
  Comparator #(.mode("unsigned"), .width(5)) comparator_7 (
    .a(inID_jtarget[25:21]), .b(Ex_Rw), .eq(comparator_7_eq));  // open: gt, lt
  Comparator #(.mode("unsigned"), .width(5)) comparator_8 (
    .a(Ex_Rw), .b(inID_jtarget[20:16]), .eq(comparator_8_eq));  // open: gt, lt
  assign bit_extender_3_out = {{14{ID_imm16[15]}}, {ID_imm16, func}};  // Bit_Extender bit_extender_3
  Multiplexer #(.width(5)) multiplexer_12 (.in0(multiplexer_11_out), .in1({5{1'b1}}), .out(ID_Rw), .sel(or_4_out));
  and and_12 (and_12_out, inID_Jump, ID_RegWr, not_3_out);
  not not_3 (not_3_out, Rtype);
  Adder #(.width(30)) adder_2 (.a(ID_nextpc), .b(bit_extender_3_out), .out(adder_2_out));  // open: cin, cout
  Bit_Extender #(.in_width(32), .out_width(8), .\type ("zero")) bit_extender_4 (.in(DRAMout), .out(bit_extender_4_out));
  Bit_Extender #(.in_width(32), .\type ("zero")) bit_extender_5 (.in(DRAMout), .out(bit_extender_5_out));
  Multiplexer #(.width(32)) multiplexer_13 (.in0({32{1'b0}}), .in1(ram_1_dout), .out(out_5), .sel(Working));
  Multiplexer #(.width(32)) multiplexer_14 (
    .in0(multiplexer_9_out), .in1(Ex_ALUout), .out(multiplexer_14_out), .sel(and_13_out));
  and and_13 (and_13_out, comparator_7_eq, Ex_RegWr);
  and and_14 (and_14_out, Ex_RegWr, comparator_8_eq);
  Multiplexer #(.width(32)) multiplexer_15 (
    .in0(multiplexer_10_out), .in1(Ex_ALUout), .out(multiplexer_15_out), .sel(and_14_out));
  Multiplexer #(.width(30)) multiplexer_16 (
    .in0(adder_2_out), .in1({ID_nextpc[29:26], inID_jtarget, ID_imm16, func}), .out(multiplexer_16_out),
    .sel(inID_Jump));
  or or_5 (Ex_WEMask[1], Ex_AAOp[0], Ex_AAOp[1]);
  xor xor_1 (Ex_WEMask[3], Ex_AAOp[0], Ex_AAOp[1]);
  nor5 nor5_1 (.wire_in(inID_jtarget[25:21]), .wire_out(nor5_1_wire_out));
  nor5 nor5_2 (.wire_in(inID_jtarget[20:16]), .wire_out(nor5_2_wire_out));
  Multiplexer #(.width(30)) multiplexer_17 (
    .in0(multiplexer_16_out), .in1(ID_BusA[31:2]), .out(fwID_jtarget), .sel(Rtype));
  ext_mux8 ext_mux8_1 (.in_8(bit_extender_4_out), .ext_op(inMem_Sel), .out_32(ext_mux8_1_out_32));
  ext_mux16 ext_mux16_1 (.in_16(bit_extender_5_out), .ext_op(inMem_Sel), .out_32(ext_mux16_1_out_32));
  Multiplexer #(.width(32)) multiplexer_18 (
    .in0(multiplexer_14_out), .in1(inID_DataA), .out(ID_BusA), .sel(nor5_1_wire_out));
  and and_15 (and_15_out, and_13_out, Ex_Mem2Reg);
  and and_16 (and_16_out, Ex_Mem2Reg, and_14_out);
  Multiplexer #(.width(32)) multiplexer_19 (
    .in0(multiplexer_15_out), .in1(inID_DataB), .out(ID_BusB), .sel(nor5_2_wire_out));
  or or_6 (ID_Branch, inID_Branch, inID_Jump);
  Multiplexer #(.select(2), .width(32)) multiplexer_20 (
    .in0(ext_mux8_1_out_32), .in1(DRAMout), .in3(ext_mux16_1_out_32), .out(Mem_BusW), .sel(inMem_AAOp));  // open: in2
  or or_7 (FlushID2, and_15_out, and_16_out);
  Bit_Extender #(.in_width(30), .out_width(8), .\type ("zero")) bit_extender_6 (
    .in(Ex_ALUout[31:2]), .out(bit_extender_6_out));
  RAM #(.byteenables("byteEnables"), .dataWidth(32), .trigger("falling")) ram_2 (
    .addr(bit_extender_6_out), .we(Ex_MemWr), .oe(Ex_Mem2Reg), .clk(clk_brp), .din(Ex_BusB), .dout(DRAMout),
    .be3(Ex_WEMask[3]), .be2(Ex_WEMask[3]), .be1(Ex_WEMask[1]), .be0(1'b1));
  Register #(.trigger("falling"), .width(30)) register_11 (
    .D(ID_nextpc), .en(n_stall_EX), .clk(clk_brp), .Q(register_11_q));  // open: clr
  Register #(.trigger("falling"), .width(32)) register_12 (
    .D(ID_BusA), .en(n_stall_EX), .clk(clk_brp), .Q(register_12_q));  // open: clr
  Register #(.trigger("falling"), .width(32)) register_13 (
    .D(ID_BusB), .en(n_stall_EX), .clk(clk_brp), .Q(Ex_BusB));  // open: clr
  Register #(.trigger("falling"), .width(16)) register_14 (
    .D({ID_imm16, func}), .en(n_stall_EX), .clk(clk_brp), .Q(register_14_q));  // open: clr
  Register #(.trigger("falling"), .width(5)) register_15 (
    .D(ID_ALUctl), .en(n_stall_EX), .clk(clk_brp), .Q(register_15_q));  // open: clr
  Register #(.trigger("falling"), .width(1)) register_16 (
    .D(ID_RegWr), .en(n_stall_EX), .clk(clk_brp), .Q(register_16_q));  // open: clr
  Register #(.trigger("falling"), .width(1)) register_17 (
    .D(ID_MemWr), .en(n_stall_EX), .clk(clk_brp), .Q(register_17_q));  // open: clr
  Register #(.trigger("falling"), .width(1)) register_18 (
    .D(ID_Mem2Reg), .en(n_stall_EX), .clk(clk_brp), .Q(Ex_Mem2Reg));  // open: clr
  Clock clock_1 (.out(clk_brp));
  Register #(.trigger("falling"), .width(1)) register_19 (
    .D(ID_ExtOp), .en(n_stall_EX), .clk(clk_brp), .Q(register_19_q));  // open: clr
  Register #(.trigger("falling"), .width(1)) register_20 (
    .D(ID_ALUimm), .en(n_stall_EX), .clk(clk_brp), .Q(register_20_q));  // open: clr
  and and_17 (Ex_RegWr, register_16_q, n_FlushEX);
  and and_18 (Ex_MemWr, register_17_q, n_FlushEX);
  or or_8 (clr_pc, in_3, in_4);
  Multiplexer #(.width(32)) multiplexer_21 (
    .in0(register_12_q), .in1({register_11_q, 2'b00}), .out(multiplexer_21_out), .sel(inEx_Branch));
  or or_9 (or_9_out, FlushID2, FlushID22);
  not not_4 (n_FlushID, or_9_out);
  not not_5 (n_FlushEX, 1'b0);
  or or_10 (or_10_out, FlushID2, stall_EX_MDU);
  or or_11 (stall_ID, FlushID2, stall_EX_MDU);
  ext_mux16 ext_mux16_2 (.in_16(register_14_q), .ext_op(register_19_q), .out_32(ext_mux16_2_out_32));
  not not_6 (n_stall_IF, or_10_out);
  not not_7 (n_stall_ID, stall_ID);
  not not_8 (n_stall_EX, stall_EX_MDU);
  not not_9 (n_stall_MEM, in_1);
  not not_10 (n_stall_WB, in_2);
  Multiplexer #(.width(32)) multiplexer_22 (
    .in0(Ex_BusB), .in1(ext_mux16_2_out_32), .out(multiplexer_22_out), .sel(register_20_q));
  Register #(.trigger("falling"), .width(5)) register_21 (
    .D(ID_imm16[10:6]), .en(n_stall_EX), .clk(clk_brp), .Q(register_21_q));  // open: clr
  Register #(.trigger("falling"), .width(5)) register_22 (
    .D(ID_Rw), .en(n_stall_EX), .clk(clk_brp), .Q(Ex_Rw));  // open: clr
  Register #(.trigger("falling"), .width(1)) register_23 (
    .D(ID_Branch), .en(n_stall_EX), .clk(clk_brp), .Q(inEx_Branch));  // open: clr
  Register #(.trigger("falling"), .width(1)) register_24 (
    .D(ID_Mov), .en(n_stall_EX), .clk(clk_brp), .Q(inEx_Mov));  // open: clr
  Multiplexer #(.width(32)) multiplexer_23 (
    .in0(multiplexer_22_out), .in1(32'h4), .out(multiplexer_23_out), .sel(inEx_Branch));
  Register #(.trigger("falling"), .width(32)) register_25 (
    .D(Mem_ALUout), .clk(clk_brp), .Q(register_25_q));  // open: en, clr
  Register #(.trigger("falling"), .width(32)) register_26 (
    .D(Mem_BusW), .clk(clk_brp), .Q(register_26_q));  // open: en, clr
  Register #(.trigger("falling"), .width(1)) register_27 (
    .D(Mem_Mem2Reg), .clk(clk_brp), .Q(register_27_q));  // open: en, clr
  Register #(.trigger("falling"), .width(1)) register_28 (
    .D(fwMem_RegWr), .clk(clk_brp), .Q(fwWB_RegWr));  // open: en, clr
  Register #(.trigger("falling"), .width(5)) register_29 (.D(fwMem_Rw), .clk(clk_brp), .Q(fwWB_Rw));  // open: en, clr
  assign bit_extender_7_out = {{31{n_FlushID}}, n_FlushID};  // Bit_Extender bit_extender_7
  ALU alu_1 (
    .in_A(multiplexer_21_out), .in_B(multiplexer_23_out), .ALUctr(register_15_q), .in_shamt(register_21_q),
    .out_Overflow(alu_1_out_overflow), .out_Result(alu_1_out_result));  // open: out_Zero
  Register #(.trigger("falling"), .width(1)) register_30 (
    .D(ID_Sel), .en(n_stall_EX), .clk(clk_brp), .Q(Ex_Sel));  // open: clr
  Register #(.trigger("falling"), .width(1)) register_31 (
    .D(ID_MovAcc), .en(n_stall_EX), .clk(clk_brp), .Q(inEx_MovAcc));  // open: clr
  assign and_19_out = out_6 & bit_extender_7_out;  // AND_Gate and_19, 32 bits wide
  MDU mdu_1 (
    .in_clk(clk_brp), .inX(ID_BusA), .inY(ID_BusB), .in_MDUop(ID_MDUop), .clear(in_3),
    .out_busy(stall_EX_MDU), .out_Lo(inEx_Lo), .out_Hi(inEx_Hi));
  Register #(.trigger("falling"), .width(32)) register_32 (
    .D(out_5), .en(n_stall_ID), .clk(clk_brp), .Q(out_6));  // open: clr
  Register #(.trigger("falling"), .width(32)) register_33 (
    .D(and_19_out), .en(n_stall_EX), .clk(clk_brp), .Q(out_7));  // open: clr
  Register #(.trigger("falling"), .width(32)) register_34 (
    .D(out_7), .en(n_stall_MEM), .clk(clk_brp), .Q(out_8));  // open: clr
  Register #(.trigger("falling"), .width(32)) register_35 (
    .D(out_8), .en(n_stall_WB), .clk(clk_brp), .Q(out_9));  // open: clr
  Multiplexer #(.width(32)) multiplexer_24 (
    .in0(alu_1_out_result), .in1(multiplexer_21_out), .out(multiplexer_24_out), .sel(inEx_Mov));
  Multiplexer #(.width(32)) multiplexer_25 (
    .in0(register_25_q), .in1(register_26_q), .out(fwWB_data), .sel(register_27_q));
  and and_20 (out_10, alu_1_out_overflow, n_FlushEX);
  Multiplexer #(.width(32)) multiplexer_26 (
    .in0(multiplexer_24_out), .in1(inEx_Acc), .out(Ex_ALUout), .sel(inEx_MovAcc));
  Multiplexer #(.width(32)) multiplexer_27 (.in0(inEx_Lo), .in1(inEx_Hi), .out(inEx_Acc), .sel(Ex_Sel));
  Register #(.trigger("falling"), .width(2)) register_36 (
    .D(ID_AAOp), .en(n_stall_EX), .clk(clk_brp), .Q(Ex_AAOp));  // open: clr

  // Other names for the same wires on the sheet: clk_ex = clk_brp; clk_id = clk_brp; clk_if = clk_brp;
  //   clk_mem = clk_brp; clk_wr = clk_brp; clr = in_3; Ex_instr[31:0] = out_7; Ex_Overflow = out_10;
  //   Ex_WEMask[2] = Ex_WEMask[3]; fwEx_ALUout[31:0] = Ex_ALUout; fwEx_Mem2Reg = Ex_Mem2Reg; fwEx_RegWr = Ex_RegWr;
  //   Mem_RegWr = fwMem_RegWr; Mem_Rw[4:0] = fwMem_Rw; ID_instr[31:0] = out_6; IF_instr[31:0] = out_5;
  //   inEx_AAOp[1:0] = Ex_AAOp; inEx_Sel = Ex_Sel; ID_imm16[5:0] = func;
  //   inID_jtarget (some bits) = {ID_nextpc[29:26], ID_imm16, func}; instr[25:0] = {inID_jtarget, ID_imm16, func};
  //   ID_shamt[4:0] = ID_imm16[10:6]; Rd[4:0] = ID_imm16[15:11]; Rt[4:0] = inID_jtarget[20:16];
  //   Rs[4:0] = inID_jtarget[25:21]; inID_nextpc[29:0] = ID_nextpc; Op[5:0] = instr; Mem_instr[31:0] = out_8;
  //   stall_ID_LoadUse = FlushID2; stall_MEM = in_1; stall_WB = in_2; Wr_instr[31:0] = out_9
endmodule

module mips_decoder (
  input  [4:0] in_Rt,
  input  [5:0] in_op,
  input  [5:0] in_func,
  output Rtype,
  output RegWr,
  output RegDst,
  output Sel,
  output ALUsrc,
  output MemtoReg,
  output MemWr,
  output Branch,
  output Jump,
  output EXTctr,
  output [1:0] AAop,
  output [2:0] BranchOp,
  output [4:0] ALUctl,
  output Mov,
  output MovAcc,
  output [3:0] MDUop
);

  wire addiu_out, and_6_out, and_8_out, and_9_out, and_10_out, and_11_out, bx_out, not_1_out, not_2_out,
       not_3_out, not_4_out, not_5_out, not_6_out, not_7_out, not_8_out, not_9_out, not_10_out, not_11_out,
       not_12_out, not_13_out, not_14_out, not_15_out, not_16_out, not_17_out, not_18_out, not_19_out,
       not_20_out, not_21_out, not_22_out, not_23_out, not_24_out, not_25_out, not_26_out, not_27_out,
       not_28_out, not_29_out, not_30_out, not_31_out, not_32_out, not_33_out, not_34_out, not_35_out,
       not_36_out, not_37_out, not_38_out, not_39_out, not_40_out, not_41_out, not_42_out, not_43_out,
       not_44_out, not_45_out, not_46_out, not_47_out, not_48_out, not_49_out, not_50_out, not_51_out,
       not_52_out, not_53_out, not_54_out, not_55_out, not_56_out, not_57_out, not_58_out, not_59_out,
       not_60_out, not_61_out, not_62_out, not_63_out, not_64_out, not_65_out, not_66_out, not_67_out,
       not_68_out, not_69_out, not_70_out, not_71_out, not_72_out, not_73_out, not_74_out, not_75_out,
       not_76_out, not_77_out, not_78_out, not_79_out, not_80_out, not_81_out, not_82_out, not_83_out,
       not_84_out, not_85_out, not_86_out, not_87_out, not_88_out, not_89_out, not_90_out, not_91_out,
       not_92_out, not_93_out, not_94_out, not_95_out, not_96_out, not_97_out, not_98_out, not_99_out,
       not_100_out, not_101_out, not_102_out, not_103_out, not_104_out, not_105_out, not_106_out,
       not_107_out, not_108_out, not_109_out, not_110_out, not_111_out, not_112_out, not_113_out,
       not_114_out, not_115_out, not_116_out, not_117_out, not_118_out, not_119_out, not_120_out,
       not_121_out, not_122_out, not_123_out, not_124_out, not_125_out, not_126_out, not_127_out,
       not_128_out, not_129_out, not_130_out, not_131_out, not_132_out, not_133_out, not_134_out,
       not_135_out, not_136_out, not_137_out, not_138_out, not_139_out, not_140_out, not_141_out,
       not_142_out, op_addi_out, op_andi_out, op_beq_out, op_bgez_out, op_bgezal_out, op_bgtz_out,
       op_blez_out, op_bltz_out, op_bltzal_out, op_bne_out, op_j_out, op_jal_out, op_jalr_out, op_jr_out,
       op_lb_out, op_lbu_out, op_lh_out, op_lhu_out, op_lui_out, op_lw_out, op_mfhi_out, op_mflo_out,
       op_movn_out, op_movz_out, op_mul_out, op_sb_out, op_sh_out, op_slti_out, op_sltiu_out, op_sw_out,
       op_xori_out, or_1_out, or_2_out, or_3_out, or_8_out, or_20_out, ori_out, SP2type, toALUsrc, toJump,
       toNonRegWr, toRegDst, toSel0, toSel1, toSel2;
  wire [3:0] multiplexer_1_out, or_4_out, pla_1_out, pla_2_out;
  wire [4:0] func2ALUop_out, multiplexer_2_out, multiplexer_3_out;

  PLA #(.in_width(6), .out_width(5), .\table ("100000 00001 # add\n100010 00101 # sub\n100011 00100 # subu\n101010 00111 # slt\n101011 00110 # sltu\n000000 00011 # sll\n100101 00010 # or\n100001 00000 # addu\n100100 01001 # and\n100110 01010 # xor\n000100 01011 # sllv\n100111 01101 # nor\n000011 01110 # sra\n000110 01111 # srlv\n000111 10000 # srav\n000010 01000 # srl")) func2ALUop (
    .in(in_func), .out(func2ALUop_out));
  not not_1 (not_1_out, in_func[5]);
  not not_2 (not_2_out, in_func[4]);
  not not_3 (not_3_out, in_func[2]);
  and op_movn (op_movn_out, not_1_out, not_2_out, in_func[3], not_3_out, in_func[1], in_func[0]);
  not not_4 (not_4_out, in_func[5]);
  not not_5 (not_5_out, in_func[4]);
  not not_6 (not_6_out, in_func[2]);
  and op_jalr (op_jalr_out, not_4_out, not_5_out, in_func[3], not_6_out, not_14_out, in_func[0]);
  not not_7 (not_7_out, in_func[5]);
  not not_8 (not_8_out, in_func[3]);
  not not_9 (not_9_out, in_func[2]);
  and op_mfhi (op_mfhi_out, not_7_out, in_func[4], not_8_out, not_9_out, not_15_out, not_16_out);
  PLA #(.in_width(6), .out_width(4), .\table ("011001 1000 # multu\n011000 1001 # mult\n010011 0001 # mtlo\n010001 0010 # mthi\n011011 1110 # divu\n011010 1111 # div")) pla_1 (
    .in(in_func), .out(pla_1_out));
  PLA #(.in_width(6), .out_width(4), .\table ("000101 1010 # msubu\n000100 1011 # msub\n000001 1100 # maddu\n000000 1101 # madd\n000010 1001 # mul")) pla_2 (
    .in(in_func), .out(pla_2_out));
  not not_10 (not_10_out, in_func[5]);
  not not_11 (not_11_out, in_func[4]);
  not not_12 (not_12_out, in_func[3]);
  not not_13 (not_13_out, in_func[2]);
  and op_mul (op_mul_out, not_10_out, not_11_out, not_12_out, not_13_out, in_func[1], not_17_out);
  and and_1 (toSel0, op_movn_out, Rtype);
  not not_14 (not_14_out, in_func[1]);
  not not_15 (not_15_out, in_func[1]);
  not not_16 (not_16_out, in_func[0]);
  and and_2 (toSel1, op_mfhi_out, Rtype);
  Multiplexer #(.width(4)) multiplexer_1 (.in0(4'b0000), .in1(pla_1_out), .out(multiplexer_1_out), .sel(Rtype));
  not not_17 (not_17_out, in_func[0]);
  Multiplexer #(.width(5)) multiplexer_2 (
    .in0({1'b0, or_4_out}), .in1(func2ALUop_out), .out(multiplexer_2_out), .sel(Rtype));
  Multiplexer #(.width(5)) multiplexer_3 (.in0(5'b10001), .in1(5'b10010), .out(multiplexer_3_out), .sel(in_func[0]));
  not not_18 (not_18_out, in_func[5]);
  not not_19 (not_19_out, in_func[4]);
  not not_20 (not_20_out, in_func[2]);
  not not_21 (not_21_out, in_func[0]);
  and op_movz (op_movz_out, not_18_out, not_19_out, in_func[3], not_20_out, in_func[1], not_21_out);
  or or_1 (or_1_out, op_movn_out, op_movz_out);
  not not_22 (not_22_out, in_func[5]);
  not not_23 (not_23_out, in_func[4]);
  not not_24 (not_24_out, in_func[2]);
  not not_25 (not_25_out, in_func[1]);
  not not_26 (not_26_out, in_func[0]);
  and op_jr (op_jr_out, not_22_out, not_23_out, in_func[3], not_24_out, not_25_out, not_26_out);
  or or_2 (or_2_out, op_jalr_out, op_jr_out);
  not not_27 (not_27_out, in_func[5]);
  not not_28 (not_28_out, in_func[3]);
  not not_29 (not_29_out, in_func[2]);
  not not_30 (not_30_out, in_func[0]);
  and op_mflo (op_mflo_out, not_27_out, in_func[4], not_28_out, not_29_out, in_func[1], not_30_out);
  or or_3 (or_3_out, op_mfhi_out, op_mflo_out);
  Multiplexer #(.width(4)) multiplexer_4 (.in0(multiplexer_1_out), .in1(pla_2_out), .out(MDUop), .sel(SP2type));
  and and_3 (toRegDst, op_mul_out, SP2type);
  not not_31 (not_31_out, in_op[5]);
  or or_4 (or_4_out[0], op_addi_out, op_andi_out, op_slti_out);
  or or_5 (or_4_out[1], op_xori_out, ori_out, op_sltiu_out, op_slti_out);
  or or_6 (or_4_out[2], op_sltiu_out, op_slti_out, op_lui_out);
  or or_7 (or_4_out[3], op_andi_out, op_xori_out, op_lui_out);
  Multiplexer #(.width(5)) multiplexer_5 (
    .in0(multiplexer_2_out), .in1(multiplexer_3_out), .out(ALUctl), .sel(SP2type));
  or or_8 (or_8_out, MDUop[0], MDUop[1], MDUop[2], MDUop[3]);
  not not_32 (not_32_out, in_op[1]);
  not not_33 (not_33_out, in_op[0]);
  and SP2_ty (SP2type, not_31_out, in_op[4], in_op[3], in_op[2], not_32_out, not_33_out);
  and and_4 (Mov, Rtype, or_1_out);
  and and_5 (toJump, Rtype, or_2_out);
  and and_6 (and_6_out, Rtype, or_3_out);
  and and_7 (toNonRegWr, or_8_out, not_34_out);
  not not_34 (not_34_out, toRegDst);
  not not_35 (not_35_out, in_op[5]);
  not not_36 (not_36_out, in_op[4]);
  not not_37 (not_37_out, in_op[3]);
  not not_38 (not_38_out, in_op[2]);
  not not_39 (not_39_out, in_op[1]);
  not not_40 (not_40_out, in_op[0]);
  and R_ty (Rtype, not_35_out, not_36_out, not_37_out, not_38_out, not_39_out, not_40_out);
  or or_9 (MovAcc, and_6_out, toRegDst);
  not not_41 (not_41_out, in_op[5]);
  not not_42 (not_42_out, in_op[4]);
  and ori (ori_out, not_41_out, not_42_out, in_op[3], in_op[2], not_44_out, in_op[0]);
  or or_10 (RegDst, Rtype, toRegDst);
  not not_43 (not_43_out, in_op[5]);
  not not_44 (not_44_out, in_op[1]);
  not not_45 (not_45_out, in_op[4]);
  not not_46 (not_46_out, in_op[1]);
  not not_47 (not_47_out, in_op[0]);
  and op_andi (op_andi_out, not_43_out, not_45_out, in_op[3], in_op[2], not_46_out, not_47_out);
  not not_48 (not_48_out, in_op[5]);
  not not_49 (not_49_out, in_op[4]);
  and op_xori (op_xori_out, not_48_out, not_49_out, in_op[3], in_op[2], in_op[1], not_50_out);
  not not_50 (not_50_out, in_op[0]);
  not not_51 (not_51_out, in_op[5]);
  not not_52 (not_52_out, in_op[4]);
  not not_53 (not_53_out, in_op[2]);
  not not_54 (not_54_out, in_op[1]);
  and addiu (addiu_out, not_51_out, not_52_out, in_op[3], not_53_out, not_54_out, in_op[0]);
  not not_55 (not_55_out, in_op[5]);
  not not_56 (not_56_out, in_op[4]);
  not not_57 (not_57_out, in_op[2]);
  not not_58 (not_58_out, in_op[1]);
  not not_59 (not_59_out, in_op[0]);
  and op_addi (op_addi_out, not_55_out, not_56_out, in_op[3], not_57_out, not_58_out, not_59_out);
  not not_60 (not_60_out, in_op[5]);
  not not_61 (not_61_out, in_op[4]);
  not not_62 (not_62_out, in_op[2]);
  and op_slti (op_slti_out, not_60_out, not_61_out, in_op[3], not_62_out, in_op[1], not_63_out);
  not not_63 (not_63_out, in_op[0]);
  not not_64 (not_64_out, in_op[5]);
  not not_65 (not_65_out, in_op[4]);
  not not_66 (not_66_out, in_op[2]);
  and op_sltiu (op_sltiu_out, not_64_out, not_65_out, in_op[3], not_66_out, in_op[1], in_op[0]);
  not not_67 (not_67_out, in_op[5]);
  not not_68 (not_68_out, in_op[4]);
  and op_lui (op_lui_out, not_67_out, not_68_out, in_op[3], in_op[2], in_op[1], in_op[0]);
  or or_11 (ALUsrc, op_xori_out, op_andi_out, ori_out, addiu_out, op_addi_out, op_slti_out, op_sltiu_out, op_lui_out, toALUsrc);
  or or_12 (EXTctr, addiu_out, op_addi_out, op_slti_out, toALUsrc);
  not not_69 (not_69_out, in_op[4]);
  not not_70 (not_70_out, in_op[3]);
  not not_71 (not_71_out, in_op[2]);
  and op_lw (op_lw_out, in_op[5], not_69_out, not_70_out, not_71_out, in_op[1], in_op[0]);
  not not_72 (not_72_out, in_op[4]);
  not not_73 (not_73_out, in_op[3]);
  not not_74 (not_74_out, in_op[2]);
  not not_75 (not_75_out, in_op[1]);
  not not_76 (not_76_out, in_op[0]);
  and op_lb (op_lb_out, in_op[5], not_72_out, not_73_out, not_74_out, not_75_out, not_76_out);
  not not_77 (not_77_out, in_op[4]);
  not not_78 (not_78_out, in_op[3]);
  and op_lh (op_lh_out, in_op[5], not_77_out, not_78_out, not_79_out, not_80_out, in_op[0]);
  not not_79 (not_79_out, in_op[2]);
  not not_80 (not_80_out, in_op[1]);
  not not_81 (not_81_out, in_op[4]);
  not not_82 (not_82_out, in_op[3]);
  not not_83 (not_83_out, in_op[1]);
  not not_84 (not_84_out, in_op[0]);
  and op_lbu (op_lbu_out, in_op[5], not_81_out, not_82_out, in_op[2], not_83_out, not_84_out);
  not not_85 (not_85_out, in_op[4]);
  not not_86 (not_86_out, in_op[3]);
  not not_87 (not_87_out, in_op[1]);
  and op_lhu (op_lhu_out, in_op[5], not_85_out, not_86_out, in_op[2], not_87_out, in_op[0]);
  or or_13 (toSel2, op_lbu_out, op_lhu_out);
  or or_14 (MemtoReg, op_lw_out, op_lb_out, op_lh_out, op_lbu_out, op_lhu_out);
  not not_88 (not_88_out, in_op[4]);
  and op_sw (op_sw_out, in_op[5], not_88_out, in_op[3], not_89_out, in_op[1], in_op[0]);
  not not_89 (not_89_out, in_op[2]);
  not not_90 (not_90_out, in_op[4]);
  not not_91 (not_91_out, in_op[2]);
  not not_92 (not_92_out, in_op[1]);
  not not_93 (not_93_out, in_op[0]);
  and op_sb (op_sb_out, in_op[5], not_90_out, in_op[3], not_91_out, not_92_out, not_93_out);
  not not_94 (not_94_out, in_op[4]);
  not not_95 (not_95_out, in_op[2]);
  not not_96 (not_96_out, in_op[1]);
  and op_sh (op_sh_out, in_op[5], not_94_out, in_op[3], not_95_out, not_96_out, in_op[0]);
  or or_15 (MemWr, op_sw_out, op_sb_out, op_sh_out);
  or or_16 (toALUsrc, MemWr, MemtoReg);
  or or_17 (AAop[0], op_lw_out, op_sw_out, op_lh_out, op_lhu_out, op_sh_out);
  or or_18 (AAop[1], op_lh_out, op_lhu_out, op_sh_out);
  not not_97 (not_97_out, in_op[5]);
  not not_98 (not_98_out, in_op[4]);
  not not_99 (not_99_out, in_op[3]);
  not not_100 (not_100_out, in_op[2]);
  not not_101 (not_101_out, in_op[0]);
  and op_j (op_j_out, not_97_out, not_98_out, not_99_out, not_100_out, in_op[1], not_101_out);
  not not_102 (not_102_out, in_op[5]);
  not not_103 (not_103_out, in_op[4]);
  not not_104 (not_104_out, in_op[3]);
  and op_jal (op_jal_out, not_102_out, not_103_out, not_104_out, not_105_out, in_op[1], in_op[0]);
  not not_105 (not_105_out, in_op[2]);
  or or_19 (Jump, op_j_out, toJump, op_jal_out);
  not not_106 (not_106_out, in_op[5]);
  not not_107 (not_107_out, in_op[4]);
  not not_108 (not_108_out, in_op[3]);
  not not_109 (not_109_out, in_op[1]);
  not not_110 (not_110_out, in_op[0]);
  and op_beq (op_beq_out, not_106_out, not_107_out, not_108_out, in_op[2], not_109_out, not_110_out);
  not not_111 (not_111_out, in_op[5]);
  not not_112 (not_112_out, in_op[4]);
  not not_113 (not_113_out, in_op[3]);
  not not_114 (not_114_out, in_op[2]);
  and bx (bx_out, not_111_out, not_112_out, not_113_out, not_114_out, not_115_out, in_op[0]);
  not not_115 (not_115_out, in_op[1]);
  and and_8 (and_8_out, bx_out, op_bgez_out);
  and op_bgez (op_bgez_out, not_116_out, not_117_out, not_118_out, not_119_out, in_Rt[0]);
  not not_116 (not_116_out, in_Rt[4]);
  not not_117 (not_117_out, in_Rt[3]);
  not not_118 (not_118_out, in_Rt[2]);
  not not_119 (not_119_out, in_Rt[1]);
  and and_9 (and_9_out, bx_out, op_bgezal_out);
  and op_bgezal (op_bgezal_out, in_Rt[4], not_120_out, not_121_out, not_122_out, in_Rt[0]);
  not not_120 (not_120_out, in_Rt[3]);
  not not_121 (not_121_out, in_Rt[2]);
  not not_122 (not_122_out, in_Rt[1]);
  not not_123 (not_123_out, in_op[5]);
  not not_124 (not_124_out, in_op[4]);
  not not_125 (not_125_out, in_op[3]);
  and op_bgtz (op_bgtz_out, not_123_out, not_124_out, not_125_out, in_op[2], in_op[1], in_op[0]);
  not not_126 (not_126_out, in_op[5]);
  not not_127 (not_127_out, in_op[4]);
  not not_128 (not_128_out, in_op[3]);
  and op_blez (op_blez_out, not_126_out, not_127_out, not_128_out, in_op[2], in_op[1], not_129_out);
  not not_129 (not_129_out, in_op[0]);
  and and_10 (and_10_out, bx_out, op_bltz_out);
  and op_bltz (op_bltz_out, not_130_out, not_131_out, not_132_out, not_133_out, not_134_out);
  not not_130 (not_130_out, in_Rt[4]);
  not not_131 (not_131_out, in_Rt[3]);
  not not_132 (not_132_out, in_Rt[2]);
  not not_133 (not_133_out, in_Rt[1]);
  not not_134 (not_134_out, in_Rt[0]);
  and and_11 (and_11_out, bx_out, op_bltzal_out);
  not not_135 (not_135_out, in_Rt[3]);
  not not_136 (not_136_out, in_op[5]);
  and op_bltzal (op_bltzal_out, in_Rt[4], not_135_out, not_137_out, not_138_out, not_139_out);
  not not_137 (not_137_out, in_Rt[2]);
  not not_138 (not_138_out, in_Rt[1]);
  not not_139 (not_139_out, in_Rt[0]);
  not not_140 (not_140_out, in_op[4]);
  not not_141 (not_141_out, in_op[3]);
  not not_142 (not_142_out, in_op[1]);
  and op_bne (op_bne_out, not_136_out, not_140_out, not_141_out, in_op[2], not_142_out, in_op[0]);
  or or_20 (or_20_out, MemWr, op_j_out, op_beq_out, and_8_out, op_bgtz_out, op_blez_out, and_10_out, op_bne_out, toNonRegWr);
  not not_143 (RegWr, or_20_out);
  or or_21 (Sel, toSel0, toSel1, toSel2);
  or or_22 (Branch, op_beq_out, bx_out, op_bgtz_out, op_blez_out, op_bne_out);
  or or_23 (BranchOp[0], and_8_out, op_bgtz_out, and_10_out, op_bne_out);
  or or_24 (BranchOp[1], and_9_out, op_bgtz_out, and_11_out, op_bne_out);
  or or_25 (BranchOp[2], op_blez_out, and_10_out, and_11_out, op_bne_out);

  // Other names for the same wires on the sheet: Op[5:0] = in_op; Rt[4:0] = in_Rt; toEXTctr = toALUsrc;
  //   toNRegWr = MemWr

  // Notes on the sheet:
  //   (clz/clo)
  //   1:imm, 0:bus
  //   1:sign, 0:zero (on imm)
endmodule

module adder32 (
  input  in_Cin,
  input  [31:0] in_A,
  input  [31:0] in_B,
  output [31:0] out_F,
  output out_SF,
  output out_Cout,
  output out_ZF,
  output out_OF
);

  wire and_1_out, and_2_out, not_1_out, not_2_out, not_3_out;

  Adder #(.width(32)) adder_1 (.a(in_A), .b(in_B), .out(out_F), .cin(in_Cin), .cout(out_Cout));
  nor32 c (.in32(out_F), .result(out_ZF));
  not not_1 (not_1_out, in_A[31]);
  not not_2 (not_2_out, in_B[31]);
  and and_1 (and_1_out, not_1_out, not_2_out, out_F[31]);
  and and_2 (and_2_out, in_A[31], in_B[31], not_3_out);
  not not_3 (not_3_out, out_F[31]);
  or or_1 (out_OF, and_1_out, and_2_out);

  assign out_SF = out_F[31];
endmodule

module nor32 (
  input  [31:0] in32,
  output result
);

  wire or_1_out;

  or or_1 (or_1_out, in32[0], in32[1], in32[2], in32[3], in32[4], in32[5], in32[6], in32[7], in32[8], in32[9], in32[10], in32[11], in32[12], in32[13], in32[14], in32[15], in32[16], in32[17], in32[18], in32[19], in32[20], in32[21], in32[22], in32[23], in32[24], in32[25], in32[26], in32[27], in32[28], in32[29], in32[30], in32[31]);
  not not_1 (result, or_1_out);
endmodule

module nor5 (
  input  [4:0] wire_in,
  output wire_out
);

  wire or_1_out;

  or or_1 (or_1_out, wire_in[0], wire_in[1], wire_in[2], wire_in[3], wire_in[4]);
  not not_1 (wire_out, or_1_out);
endmodule

module ALU (
  input  [31:0] in_A,
  input  [31:0] in_B,
  input  [4:0] ALUctr,
  input  [4:0] in_shamt,
  output out_Zero,
  output out_Overflow,
  output [31:0] out_Result
);

  wire Adder_out_cout, Adder_out_of, Adder_out_sf, clz_1_wire_q, not_1_out, OVctl, SIGctl, SUBctl, xor_3_out;
  wire [3:0] OPcode;
  wire [4:0] clz_1_wire_out, multiplexer_1_out;
  wire [31:0] adder, and_out, bit_extender_1_out, bit_extender_2_out, bit_extender_5_out, clz_out, nor_out,
       or_out, shift_left_16, sll_out, slt, sltu, sra_out, srl_out, xor_1_out, xor_4_out, xor_out;

  assign or_out = in_A | in_B;  // OR_Gate or_1, 32 bits wide
  assign nor_out = ~(in_A | in_B);  // NOR_Gate nor_1, 32 bits wide
  Shifter #(.width(32)) shifter_1 (.in(in_B), .\dist (5'b10000), .out(shift_left_16));
  assign bit_extender_1_out = {{31{SUBctl}}, SUBctl};  // Bit_Extender bit_extender_1
  Multiplexer #(.width(5)) multiplexer_1 (.in0(in_shamt), .in1(in_A[4:0]), .out(multiplexer_1_out), .sel(SIGctl));
  ALU_dec ALU_decoder (.in_op(ALUctr), .SUB(SUBctl), .OV(OVctl), .SIG(SIGctl), .OP(OPcode));
  assign xor_1_out = in_B ^ bit_extender_1_out;  // XOR_Gate xor_1, 32 bits wide
  assign xor_out = in_A ^ in_B;  // XOR_Gate xor_2, 32 bits wide
  assign and_out = in_A & in_B;  // AND_Gate and_1, 32 bits wide
  Shifter #(.width(32)) shifter_2 (.in(in_B), .\dist (multiplexer_1_out), .out(sll_out));
  Shifter #(.shift("lr"), .width(32)) shifter_3 (.in(in_B), .\dist (multiplexer_1_out), .out(srl_out));
  Shifter #(.shift("ar"), .width(32)) shifter_4 (.in(in_B), .\dist (multiplexer_1_out), .out(sra_out));
  Multiplexer #(.select(4), .width(32)) multiplexer_2 (
    .in0(adder), .in1(or_out), .in2(slt), .in3(sll_out), .in4(srl_out), .in5(and_out), .in6(xor_out),
    .in7(shift_left_16), .in8(sra_out), .in9(nor_out), .in10(clz_out), .in11(sltu), .out(out_Result),
    .sel(OPcode));  // open: in12, in13, in14, in15
  adder32 u_Adder (
    .in_Cin(SUBctl), .in_A(in_A), .in_B(xor_1_out), .out_F(adder), .out_SF(Adder_out_sf),
    .out_Cout(Adder_out_cout), .out_ZF(out_Zero), .out_OF(Adder_out_of));
  xor xor_3 (xor_3_out, Adder_out_sf, Adder_out_of);
  not not_1 (not_1_out, Adder_out_cout);
  assign bit_extender_2_out = {{31{SIGctl}}, SIGctl};  // Bit_Extender bit_extender_2
  assign sltu = {{31{1'b0}}, not_1_out};  // Bit_Extender bit_extender_3
  assign slt = {{31{1'b0}}, xor_3_out};  // Bit_Extender bit_extender_4
  assign xor_4_out = in_A ^ bit_extender_2_out;  // XOR_Gate xor_4, 32 bits wide
  clz clz_1 (.wire_in(xor_4_out), .wire_Q(clz_1_wire_q), .wire_out(clz_1_wire_out));
  assign bit_extender_5_out = {{27{1'b0}}, clz_1_wire_out};  // Bit_Extender bit_extender_5
  and and_2 (out_Overflow, Adder_out_of, OVctl);
  Multiplexer #(.width(32)) multiplexer_3 (.in0(bit_extender_5_out), .in1(32'h100), .out(clz_out), .sel(clz_1_wire_q));

  // Other names for the same wires on the sheet: inA[31:0] = in_A; inB[31:0] = in_B
endmodule

module ALU_dec (
  input  [4:0] in_op,
  output SUB,
  output OV,
  output SIG,
  output [3:0] OP
);

  wire decoder_1_out0, decoder_1_out1, decoder_1_out2, decoder_1_out3, decoder_1_out4, decoder_1_out5,
       decoder_1_out6, decoder_1_out7, decoder_1_out8, decoder_1_out9, decoder_1_out10, decoder_1_out11,
       decoder_1_out12, decoder_1_out13, decoder_1_out14, decoder_1_out15, decoder_1_out16, decoder_1_out17,
       decoder_1_out18;

  Decoder #(.select(5)) decoder_1 (
    .out0(decoder_1_out0), .out1(decoder_1_out1), .out2(decoder_1_out2), .out3(decoder_1_out3),
    .out4(decoder_1_out4), .out5(decoder_1_out5), .out6(decoder_1_out6), .out7(decoder_1_out7),
    .out8(decoder_1_out8), .out9(decoder_1_out9), .out10(decoder_1_out10), .out11(decoder_1_out11),
    .out12(decoder_1_out12), .out13(decoder_1_out13), .out14(decoder_1_out14), .out15(decoder_1_out15),
    .out16(decoder_1_out16), .out17(decoder_1_out17), .out18(decoder_1_out18), .sel(in_op));  // open: out19, out20, out21, out22, out23, out24, out25, out26, out27, out28, out29, out30, out31, en
  or or_1 (SUB, decoder_1_out4, decoder_1_out5, decoder_1_out6, decoder_1_out7);
  or or_2 (OV, decoder_1_out1, decoder_1_out5);
  or or_3 (SIG, decoder_1_out16, decoder_1_out15, decoder_1_out11, decoder_1_out18);
  or or_4 (OP[0], decoder_1_out6, decoder_1_out2, decoder_1_out3, decoder_1_out9, decoder_1_out11, decoder_1_out12, decoder_1_out13);
  or or_5 (OP[1], decoder_1_out6, decoder_1_out7, decoder_1_out3, decoder_1_out10, decoder_1_out11, decoder_1_out12, decoder_1_out17, decoder_1_out18);
  or or_6 (OP[2], decoder_1_out8, decoder_1_out9, decoder_1_out10, decoder_1_out12, decoder_1_out8, decoder_1_out15);
  or or_7 (OP[3], decoder_1_out6, decoder_1_out13, decoder_1_out14, decoder_1_out16, decoder_1_out17, decoder_1_out18);
endmodule

module reg32 (
  input  clear,
  input  [4:0] in_Ra,
  input  [4:0] in_Rb,
  input  [4:0] in_Rw,
  input  in_WE,
  input  [31:0] in_Rwdata,
  input  clk,
  output [31:0] out_Ra,
  output [31:0] out_Rb
);

  wire decoder_1_out0, decoder_1_out1, decoder_1_out2, decoder_1_out3;
  wire [31:0] reg8_0locked_1_out_r1data, reg8_0locked_1_out_r2data, reg8_1_out_r1data, reg8_1_out_r2data,
       reg8_2_out_r1data, reg8_2_out_r2data, reg8_3_out_r1data, reg8_3_out_r2data;

  Decoder #(.select(2)) decoder_1 (
    .out0(decoder_1_out0), .out1(decoder_1_out1), .out2(decoder_1_out2), .out3(decoder_1_out3),
    .sel(in_Rw[4:3]), .en(in_WE));
  reg8_0locked reg8_0locked_1 (
    .in_Rwdata(in_Rwdata), .clk(clk), .in_WE(decoder_1_out0), .in_Rwaddr(in_Rw[2:0]), .clear(clear),
    .in_R1addr(in_Ra[2:0]), .in_R2addr(in_Rb[2:0]), .out_R1data(reg8_0locked_1_out_r1data),
    .out_R2data(reg8_0locked_1_out_r2data));
  reg8 reg8_1 (
    .in_Rwdata(in_Rwdata), .clk(clk), .in_WE(decoder_1_out1), .in_Rwaddr(in_Rw[2:0]), .clear(clear),
    .in_R1addr(in_Ra[2:0]), .in_R2addr(in_Rb[2:0]), .out_R1data(reg8_1_out_r1data),
    .out_R2data(reg8_1_out_r2data));
  reg8 reg8_2 (
    .in_Rwdata(in_Rwdata), .clk(clk), .in_WE(decoder_1_out2), .in_Rwaddr(in_Rw[2:0]), .clear(clear),
    .in_R1addr(in_Ra[2:0]), .in_R2addr(in_Rb[2:0]), .out_R1data(reg8_2_out_r1data),
    .out_R2data(reg8_2_out_r2data));
  reg8 reg8_3 (
    .in_Rwdata(in_Rwdata), .clk(clk), .in_WE(decoder_1_out3), .in_Rwaddr(in_Rw[2:0]), .clear(clear),
    .in_R1addr(in_Ra[2:0]), .in_R2addr(in_Rb[2:0]), .out_R1data(reg8_3_out_r1data),
    .out_R2data(reg8_3_out_r2data));
  Multiplexer #(.select(2), .width(32)) multiplexer_1 (
    .in0(reg8_0locked_1_out_r1data), .in1(reg8_1_out_r1data), .in2(reg8_2_out_r1data),
    .in3(reg8_3_out_r1data), .out(out_Ra), .sel(in_Ra[4:3]));
  Multiplexer #(.select(2), .width(32)) multiplexer_2 (
    .in0(reg8_0locked_1_out_r2data), .in1(reg8_1_out_r2data), .in2(reg8_2_out_r2data),
    .in3(reg8_3_out_r2data), .out(out_Rb), .sel(in_Rb[4:3]));
endmodule

module reg8 (
  input  [31:0] in_Rwdata,
  input  clk,
  input  in_WE,
  input  [2:0] in_Rwaddr,
  input  clear,
  input  [2:0] in_R1addr,
  input  [2:0] in_R2addr,
  output [31:0] out_R1data,
  output [31:0] out_R2data
);

  wire decoder_1_out0, decoder_1_out1, decoder_1_out2, decoder_1_out3, decoder_1_out4, decoder_1_out5,
       decoder_1_out6, decoder_1_out7;
  wire [31:0] reg0_q, reg1_q, reg2_q, reg3_q, reg4_q, reg5_q, reg6_q, reg7_q;

  Decoder #(.select(3)) decoder_1 (
    .out0(decoder_1_out0), .out1(decoder_1_out1), .out2(decoder_1_out2), .out3(decoder_1_out3),
    .out4(decoder_1_out4), .out5(decoder_1_out5), .out6(decoder_1_out6), .out7(decoder_1_out7),
    .sel(in_Rwaddr), .en(in_WE));
  Register #(.trigger("falling"), .width(32)) reg0 (
    .D(in_Rwdata), .en(decoder_1_out0), .clk(clk), .Q(reg0_q), .clr(clear));
  Register #(.trigger("falling"), .width(32)) reg1 (
    .D(in_Rwdata), .en(decoder_1_out1), .clk(clk), .Q(reg1_q), .clr(clear));
  Register #(.trigger("falling"), .width(32)) reg2 (
    .D(in_Rwdata), .en(decoder_1_out2), .clk(clk), .Q(reg2_q), .clr(clear));
  Register #(.trigger("falling"), .width(32)) reg3 (
    .D(in_Rwdata), .en(decoder_1_out3), .clk(clk), .Q(reg3_q), .clr(clear));
  Register #(.trigger("falling"), .width(32)) reg4 (
    .D(in_Rwdata), .en(decoder_1_out4), .clk(clk), .Q(reg4_q), .clr(clear));
  Register #(.trigger("falling"), .width(32)) reg5 (
    .D(in_Rwdata), .en(decoder_1_out5), .clk(clk), .Q(reg5_q), .clr(clear));
  Register #(.trigger("falling"), .width(32)) reg6 (
    .D(in_Rwdata), .en(decoder_1_out6), .clk(clk), .Q(reg6_q), .clr(clear));
  Register #(.trigger("falling"), .width(32)) reg7 (
    .D(in_Rwdata), .en(decoder_1_out7), .clk(clk), .Q(reg7_q), .clr(clear));
  Multiplexer #(.select(3), .width(32)) multiplexer_1 (
    .in0(reg0_q), .in1(reg1_q), .in2(reg2_q), .in3(reg3_q), .in4(reg4_q), .in5(reg5_q), .in6(reg6_q),
    .in7(reg7_q), .out(out_R1data), .sel(in_R1addr));
  Multiplexer #(.select(3), .width(32)) multiplexer_2 (
    .in0(reg0_q), .in1(reg1_q), .in2(reg2_q), .in3(reg3_q), .in4(reg4_q), .in5(reg5_q), .in6(reg6_q),
    .in7(reg7_q), .out(out_R2data), .sel(in_R2addr));
endmodule

module reg8_0locked (
  input  [31:0] in_Rwdata,
  input  clk,
  input  in_WE,
  input  [2:0] in_Rwaddr,
  input  clear,
  input  [2:0] in_R1addr,
  input  [2:0] in_R2addr,
  output [31:0] out_R1data,
  output [31:0] out_R2data
);

  wire decoder_1_out1, decoder_1_out2, decoder_1_out3, decoder_1_out4, decoder_1_out5, decoder_1_out6,
       decoder_1_out7;
  wire [31:0] reg0_q, reg1_q, reg2_q, reg3_q, reg4_q, reg5_q, reg6_q, reg7_q;

  Decoder #(.select(3)) decoder_1 (
    .out1(decoder_1_out1), .out2(decoder_1_out2), .out3(decoder_1_out3), .out4(decoder_1_out4),
    .out5(decoder_1_out5), .out6(decoder_1_out6), .out7(decoder_1_out7), .sel(in_Rwaddr), .en(in_WE));  // open: out0
  Register #(.trigger("falling"), .width(32)) reg0 (.clk(clk), .Q(reg0_q), .clr(1'b1));  // open: D, en
  Register #(.trigger("falling"), .width(32)) reg1 (
    .D(in_Rwdata), .en(decoder_1_out1), .clk(clk), .Q(reg1_q), .clr(clear));
  Register #(.trigger("falling"), .width(32)) reg2 (
    .D(in_Rwdata), .en(decoder_1_out2), .clk(clk), .Q(reg2_q), .clr(clear));
  Register #(.trigger("falling"), .width(32)) reg3 (
    .D(in_Rwdata), .en(decoder_1_out3), .clk(clk), .Q(reg3_q), .clr(clear));
  Register #(.trigger("falling"), .width(32)) reg4 (
    .D(in_Rwdata), .en(decoder_1_out4), .clk(clk), .Q(reg4_q), .clr(clear));
  Register #(.trigger("falling"), .width(32)) reg5 (
    .D(in_Rwdata), .en(decoder_1_out5), .clk(clk), .Q(reg5_q), .clr(clear));
  Register #(.trigger("falling"), .width(32)) reg6 (
    .D(in_Rwdata), .en(decoder_1_out6), .clk(clk), .Q(reg6_q), .clr(clear));
  Register #(.trigger("falling"), .width(32)) reg7 (
    .D(in_Rwdata), .en(decoder_1_out7), .clk(clk), .Q(reg7_q), .clr(clear));
  Multiplexer #(.select(3), .width(32)) multiplexer_1 (
    .in0(reg0_q), .in1(reg1_q), .in2(reg2_q), .in3(reg3_q), .in4(reg4_q), .in5(reg5_q), .in6(reg6_q),
    .in7(reg7_q), .out(out_R1data), .sel(in_R1addr));
  Multiplexer #(.select(3), .width(32)) multiplexer_2 (
    .in0(reg0_q), .in1(reg1_q), .in2(reg2_q), .in3(reg3_q), .in4(reg4_q), .in5(reg5_q), .in6(reg6_q),
    .in7(reg7_q), .out(out_R2data), .sel(in_R2addr));
endmodule

module ext_mux16 (
  input  [15:0] in_16,
  input  ext_op,
  output [31:0] out_32
);

  wire [31:0] bit_extender_1_out, bit_extender_2_out;

  assign bit_extender_1_out = {{16{1'b0}}, in_16};  // Bit_Extender bit_extender_1
  assign bit_extender_2_out = {{16{in_16[15]}}, in_16};  // Bit_Extender bit_extender_2
  Multiplexer #(.width(32)) multiplexer_1 (
    .in0(bit_extender_1_out), .in1(bit_extender_2_out), .out(out_32), .sel(ext_op));
endmodule

module ext_mux8 (
  input  [7:0] in_8,
  input  ext_op,
  output [31:0] out_32
);

  wire [31:0] bit_extender_1_out, bit_extender_2_out;

  assign bit_extender_1_out = {{24{1'b0}}, in_8};  // Bit_Extender bit_extender_1
  assign bit_extender_2_out = {{24{in_8[7]}}, in_8};  // Bit_Extender bit_extender_2
  Multiplexer #(.width(32)) multiplexer_1 (
    .in0(bit_extender_1_out), .in1(bit_extender_2_out), .out(out_32), .sel(ext_op));
endmodule

module branch_predictor (
  input  result,
  input  WE,
  input  clk,
  input  clr,
  output prediction
);

  wire and_1_out;
  wire [0:0] register_1_q;
  wire [1:1] multiplexer_1_out;

  Register #(.trigger("falling"), .width(2)) register_1 (
    .D({multiplexer_1_out[1], result}), .en(WE), .clk(clk), .Q({prediction, register_1_q[0]}), .clr(clr));
  Multiplexer multiplexer_1 (.in0(prediction), .in1(result), .out(multiplexer_1_out[1]), .sel(and_1_out));
  and and_1 (and_1_out, result, register_1_q[0]);
endmodule

module BNE (
  input  in0,
  input  in1,
  input  in2,
  input  in3,
  input  in4,
  input  in5,
  input  in6,
  input  in7,
  output Q,
  output [2:0] y
);

  wire and_1_out, and_2_out, and_4_out, and_5_out, not_1_out, not_2_out, not_3_out, not_4_out, not_5_out,
       or_1_out, or_2_out, or_3_out;

  not not_1 (not_1_out, in1);
  and and_1 (and_1_out, in2, not_2_out);
  not not_2 (not_2_out, in3);
  not not_3 (not_3_out, in5);
  and and_2 (and_2_out, in5, in4);
  not not_4 (not_4_out, in3);
  or or_1 (or_1_out, and_2_out, not_4_out, not_5_out);
  not not_5 (not_5_out, in2);
  and and_3 (Q, in0, in1, in2, in3, in4, in5, in6, in7);
  and and_4 (and_4_out, in0, or_2_out);
  or or_2 (or_2_out, not_1_out, and_1_out);
  and and_5 (and_5_out, in0, in2, in4, or_3_out);
  or or_3 (or_3_out, not_3_out, in6);
  and and_6 (y[1], in3, in2, in1, in0);
  and and_7 (y[2], or_1_out, in1, in0);
  or or_4 (y[0], and_4_out, and_5_out);
endmodule

module NLC (
  input  in0,
  input  in1,
  input  in2,
  input  in3,
  output a,
  output [1:0] Z
);

  wire and_1_out, not_1_out, or_1_out;

  not not_1 (not_1_out, in2);
  and and_1 (and_1_out, not_1_out, in1);
  or or_1 (or_1_out, in0, in1, in2, in3);
  not not_2 (a, or_1_out);
  nor nor_1 (Z[0], and_1_out, in3);
  nor nor_2 (Z[1], in2, in3);
endmodule

module clz (
  input  [31:0] wire_in,
  output wire_Q,
  output [4:0] wire_out
);

  wire nlc_1_a, nlc_2_a, nlc_3_a, nlc_4_a, nlc_5_a, nlc_6_a, nlc_7_a, nlc_8_a;
  wire [1:0] nlc_1_z, nlc_2_z, nlc_3_z, nlc_4_z, nlc_5_z, nlc_6_z, nlc_7_z, nlc_8_z;

  NLC nlc_1 (.in0(wire_in[28]), .in1(wire_in[29]), .in2(wire_in[30]), .in3(wire_in[31]), .a(nlc_1_a), .Z(nlc_1_z));
  NLC nlc_2 (.in0(wire_in[24]), .in1(wire_in[25]), .in2(wire_in[26]), .in3(wire_in[27]), .a(nlc_2_a), .Z(nlc_2_z));
  NLC nlc_3 (.in0(wire_in[20]), .in1(wire_in[21]), .in2(wire_in[22]), .in3(wire_in[23]), .a(nlc_3_a), .Z(nlc_3_z));
  NLC nlc_4 (.in0(wire_in[16]), .in1(wire_in[17]), .in2(wire_in[18]), .in3(wire_in[19]), .a(nlc_4_a), .Z(nlc_4_z));
  NLC nlc_5 (.in0(wire_in[12]), .in1(wire_in[13]), .in2(wire_in[14]), .in3(wire_in[15]), .a(nlc_5_a), .Z(nlc_5_z));
  NLC nlc_6 (.in0(wire_in[8]), .in1(wire_in[9]), .in2(wire_in[10]), .in3(wire_in[11]), .a(nlc_6_a), .Z(nlc_6_z));
  NLC nlc_7 (.in0(wire_in[4]), .in1(wire_in[5]), .in2(wire_in[6]), .in3(wire_in[7]), .a(nlc_7_a), .Z(nlc_7_z));
  NLC nlc_8 (.in0(wire_in[0]), .in1(wire_in[1]), .in2(wire_in[2]), .in3(wire_in[3]), .a(nlc_8_a), .Z(nlc_8_z));
  Multiplexer #(.select(3), .width(2)) multiplexer_1 (
    .in0(nlc_1_z), .in1(nlc_2_z), .in2(nlc_3_z), .in3(nlc_4_z), .in4(nlc_5_z), .in5(nlc_6_z), .in6(nlc_7_z),
    .in7(nlc_8_z), .out(wire_out[1:0]), .sel(wire_out[4:2]));
  BNE bne_1 (
    .in0(nlc_1_a), .in1(nlc_2_a), .in2(nlc_3_a), .in3(nlc_4_a), .in4(nlc_5_a), .in5(nlc_6_a), .in6(nlc_7_a),
    .in7(nlc_8_a), .Q(wire_Q), .y(wire_out[4:2]));
endmodule

module multiplier32u (
  input  [31:0] inX,
  input  [31:0] inY,
  output [63:0] outResult
);

  Multiplier #(.width(64)) multiplier_1 (
    .a({{32{1'b0}}, inX}), .b({{32{1'b0}}, inY}), .out(outResult));  // open: cin, cout

  // Other names for the same wires on the sheet: X[31:0] = inX; Y[31:0] = inY
endmodule

module multiplier32s (
  input  [31:0] inX,
  input  [31:0] inY,
  output [63:0] outResult
);

  wire [63:0] bit_extender_1_out, bit_extender_2_out;

  assign bit_extender_1_out = {{32{inX[31]}}, inX};  // Bit_Extender bit_extender_1
  assign bit_extender_2_out = {{32{inY[31]}}, inY};  // Bit_Extender bit_extender_2
  Multiplier #(.mode("twosComplement"), .width(64)) multiplier_1 (
    .a(bit_extender_1_out), .b(bit_extender_2_out), .out(outResult));  // open: cin, cout

  // Other names for the same wires on the sheet: X[31:0] = inX; Y[31:0] = inY
endmodule

module divider32u (
  input  [31:0] dividend,
  input  [31:0] divisor,
  output [31:0] result,
  output [31:0] remainder
);

  Divider #(.width(32)) divider_1 (.a(dividend), .b(divisor), .out(result), .upper({32{1'b0}}), .rem(remainder));
endmodule

module divider32s (
  input  [31:0] dividend,
  input  [31:0] divisor,
  output [31:0] result,
  output [31:0] remainder
);

  Divider #(.mode("twosComplement"), .width(32)) divider_1 (
    .a(dividend), .b(divisor), .out(result), .upper({32{1'b0}}), .rem(remainder));
endmodule

module MDU (
  input  in_clk,
  input  [31:0] inX,
  input  [31:0] inY,
  input  [3:0] in_MDUop,
  input  clear,
  output out_busy,
  output [31:0] out_Lo,
  output [31:0] out_Hi
);

  wire and_3_out, MovHi, MovLo, not_1_out, not_2_out, not_3_out, not_4_out, not_5_out, not_6_out, or_2_out,
       or_3_out, Sign, WorkDone, WrEn;
  wire [1:0] cycles_q, OpSel;
  wire [2:0] multiplexer_3_out, shifter_1_out;
  wire [31:0] Acc, multiplexer_5_out, multiplexer_6_out, X, Y;
  wire [63:0] adder_1_out, multiplexer_1_out, multiplexer_2_out, multiplexer_4_out, ResultDiv, ResultDivu,
       ResultMult, ResultMultu, subtractor_1_out;

  Register #(.trigger("falling"), .width(3)) cycles (
    .D(multiplexer_3_out), .clk(in_clk), .Q({WorkDone, cycles_q}));  // open: en, clr
  not not_1 (not_1_out, out_busy);
  not not_2 (not_2_out, in_MDUop[3]);
  Register #(.trigger("falling"), .width(4)) op (
    .D(in_MDUop), .en(not_3_out), .clk(in_clk), .Q({WrEn, OpSel, Sign}));  // open: clr
  not not_3 (not_3_out, out_busy);
  Multiplexer #(.width(64)) multiplexer_1 (.in0(ResultMultu), .in1(ResultMult), .out(multiplexer_1_out), .sel(Sign));
  Multiplexer #(.width(64)) multiplexer_2 (.in0(ResultDivu), .in1(ResultDiv), .out(multiplexer_2_out), .sel(Sign));
  and and_1 (MovLo, not_1_out, not_2_out, in_MDUop[0]);
  and and_2 (MovHi, not_1_out, not_2_out, in_MDUop[1]);
  Shifter #(.width(3)) shifter_1 (.in({WorkDone, cycles_q}), .\dist (2'b01), .out(shifter_1_out));
  and and_3 (and_3_out, in_MDUop[3], not_4_out);
  not not_4 (not_4_out, out_busy);
  Subtractor #(.width(64)) subtractor_1 (
    .a({out_Hi, Acc}), .b(multiplexer_1_out), .out(subtractor_1_out));  // open: bin, bout
  Adder #(.width(64)) adder_1 (.a({out_Hi, Acc}), .b(multiplexer_1_out), .out(adder_1_out));  // open: cin, cout
  or or_1 (out_busy, cycles_q[0], cycles_q[1]);
  Multiplexer #(.width(3)) multiplexer_3 (.in0(shifter_1_out), .in1(3'b001), .out(multiplexer_3_out), .sel(and_3_out));
  Register #(.trigger("falling"), .width(32)) register_1 (.D(inX), .en(not_5_out), .clk(in_clk), .Q(X));  // open: clr
  not not_5 (not_5_out, out_busy);
  Multiplexer #(.select(2), .width(64)) multiplexer_4 (
    .in0(multiplexer_1_out), .in1(subtractor_1_out), .in2(adder_1_out), .in3(multiplexer_2_out),
    .out(multiplexer_4_out), .sel(OpSel));
  multiplier32u multiplier32u_1 (.inX(X), .inY(Y), .outResult(ResultMultu));
  multiplier32s multiplier32s_1 (.inX(X), .inY(Y), .outResult(ResultMult));
  Multiplexer #(.width(32)) multiplexer_5 (
    .in0(multiplexer_4_out[31:0]), .in1(inX), .out(multiplexer_5_out), .sel(MovLo));
  or or_2 (or_2_out, WorkDone, MovLo);
  Multiplexer #(.width(32)) multiplexer_6 (
    .in0(multiplexer_4_out[63:32]), .in1(inX), .out(multiplexer_6_out), .sel(MovHi));
  or or_3 (or_3_out, WorkDone, MovHi);
  Register #(.trigger("falling"), .width(32)) register_2 (.D(inY), .en(not_6_out), .clk(in_clk), .Q(Y));  // open: clr
  not not_6 (not_6_out, out_busy);
  Register #(.trigger("falling"), .width(32)) Lo (
    .D(multiplexer_5_out), .en(or_2_out), .clk(in_clk), .Q(Acc), .clr(clear));
  Register #(.trigger("falling"), .width(32)) Hi (
    .D(multiplexer_6_out), .en(or_3_out), .clk(in_clk), .Q(out_Hi), .clr(clear));
  divider32u divider32u_1 (.dividend(X), .divisor(Y), .result(ResultDivu[31:0]), .remainder(ResultDivu[63:32]));
  divider32s divider32s_1 (.dividend(X), .divisor(Y), .result(ResultDiv[31:0]), .remainder(ResultDiv[63:32]));
  Multiplexer #(.width(32)) multiplexer_7 (.in0(Acc), .in1(multiplexer_5_out), .out(out_Lo), .sel(WorkDone));

  // Other names for the same wires on the sheet: Lo[31:0] = Acc; Acc[63:32] = out_Hi; Hi[31:0] = out_Hi;
  //   Busy = out_busy; clk = in_clk; inOp[3:0] = in_MDUop; inOpCode[2:0] = in_MDUop[2:0]; inWrEn = in_MDUop[3]

  // Notes on the sheet:
  //   solve mul-use hazard
endmodule
