// Logisim project multipliers.circ as structural Verilog
module CSA4 (
  input  [3:0] inX,
  input  [3:0] inY,
  input  [3:0] Cin,
  output [3:0] Cout,
  output [3:0] Result
);

  Adder #(.width(1)) adder_1 (.a(inX[0]), .b(inY[0]), .out(Result[0]), .cin(Cin[0]), .cout(Cout[1]));
  Adder #(.width(1)) adder_2 (.a(inX[1]), .b(inY[1]), .out(Result[1]), .cin(Cin[1]), .cout(Cout[0]));
  Adder #(.width(1)) adder_3 (.a(inX[2]), .b(inY[2]), .out(Result[2]), .cin(Cin[2]), .cout(Cout[2]));
  Adder #(.width(1)) adder_4 (.a(inX[3]), .b(inY[3]), .out(Result[3]), .cin(Cin[3]), .cout(Cout[3]));

  // Other names for the same wires on the sheet: c0 = Cin[0]; c1 = Cin[1]; c2 = Cin[2]; c3 = Cin[3]; x0 = inX[0];
  //   x1 = inX[1]; x2 = inX[2]; x3 = inX[3]; y0 = inY[0]; y1 = inY[1]; y2 = inY[2]; y3 = inY[3]
endmodule

module ArrayMultiplier4x4u (
  input  [3:0] inX,
  input  [3:0] inY,
  output [7:0] out_3,
  output [7:0] out_4,
  output [7:0] out_5,
  output [7:0] out_6
);

  wire adder_1_cout, adder_2_cout, adder_2_out, adder_3_cout, adder_3_out, adder_4_cout, adder_4_out,
       adder_5_cout, adder_6_cout, adder_7_cout, adder_7_out, adder_8_cout, adder_8_out, adder_9_cout,
       adder_9_out, adder_10_cout, adder_13_cout, adder_14_cout, adder_14_out, adder_15_cout, adder_15_out,
       adder_16_cout, adder_16_out, adder_19_cout, adder_20_cout, adder_21_cout, and_1_out, and_2_out,
       and_3_out, and_4_out, and_5_out, and_6_out, and_7_out, and_8_out, and_9_out, and_10_out, and_11_out,
       and_12_out, and_13_out, and_14_out, and_15_out, and_16_out, t3c_1_tout, t3c_2_tout;
  wire [0:0] adder_17_cout;
  wire [1:0] t3c_1_sel, t3c_2_sel;
  wire [3:0] bit_extender_2_out, csa4_1_cout, csa4_1_result, csa4_2_cout, csa4_2_result, multiplexer_2_out,
       multiplexer_4_out, multiplexer_5_out, multiplexer_6_out, multiplexer_7_out, multiplexer_8_out,
       multiplexer_11_out, xor_1_out;
  wire [3:1] adder_11_out, adder_12_out, multiplexer_1_out, multiplexer_3_out;
  wire [3:3] adder_11_cout, adder_12_cout;
  wire [4:0] bit_extender_1_out, multiplexer_9_out, multiplexer_10_out, negX;
  wire [4:2] adder_24_out, adder_25_out;

  Multiplexer #(.width(4)) multiplexer_1 (.in0(4'b0000), .in1(inX), .out({multiplexer_1_out, out_6[0]}), .sel(inY[0]));
  Multiplexer #(.width(4)) multiplexer_2 (.in0(4'b0000), .in1(inX), .out(multiplexer_2_out), .sel(inY[1]));
  Multiplexer #(.width(4)) multiplexer_3 (.in0(4'b0000), .in1(inX), .out({multiplexer_3_out, out_4[0]}), .sel(inY[0]));
  and and_1 (and_1_out, inX[0], inY[0]);
  Adder #(.width(1)) adder_1 (.a(and_1_out), .b(1'b0), .out(out_5[0]), .cout(adder_1_cout));  // open: cin
  and and_2 (and_2_out, inX[1], inY[0]);
  Adder #(.width(1)) adder_2 (.a(and_2_out), .b(1'b0), .out(adder_2_out), .cin(adder_1_cout), .cout(adder_2_cout));
  and and_3 (and_3_out, inX[2], inY[0]);
  Adder #(.width(1)) adder_3 (.a(and_3_out), .b(1'b0), .out(adder_3_out), .cin(adder_2_cout), .cout(adder_3_cout));
  and and_4 (and_4_out, inX[3], inY[0]);
  Adder #(.width(1)) adder_4 (.a(and_4_out), .b(1'b0), .out(adder_4_out), .cin(adder_3_cout), .cout(adder_4_cout));
  Multiplexer #(.width(4)) multiplexer_4 (.in0(4'b0000), .in1(inX), .out(multiplexer_4_out), .sel(inY[2]));
  assign xor_1_out = 4'b1111 ^ inX;  // XOR_Gate xor_1, 4 bits wide
  Adder #(.width(4)) adder_5 (.a(xor_1_out), .b(4'b0000), .out(negX[3:0]), .cin(1'b1), .cout(adder_5_cout));
  not not_1 (negX[4], adder_5_cout);
  Multiplexer #(.width(4)) multiplexer_5 (.in0(4'b0000), .in1(inX), .out(multiplexer_5_out), .sel(inY[1]));
  and and_5 (and_5_out, inX[0], inY[1]);
  Adder #(.width(1)) adder_6 (.a(and_5_out), .b(adder_2_out), .out(out_5[1]), .cout(adder_6_cout));  // open: cin
  and and_6 (and_6_out, inX[1], inY[1]);
  Adder #(.width(1)) adder_7 (
    .a(and_6_out), .b(adder_3_out), .out(adder_7_out), .cin(adder_6_cout), .cout(adder_7_cout));
  and and_7 (and_7_out, inX[2], inY[1]);
  Adder #(.width(1)) adder_8 (
    .a(and_7_out), .b(adder_4_out), .out(adder_8_out), .cin(adder_7_cout), .cout(adder_8_cout));
  and and_8 (and_8_out, inX[3], inY[1]);
  Adder #(.width(1)) adder_9 (
    .a(and_8_out), .b(adder_4_cout), .out(adder_9_out), .cin(adder_8_cout), .cout(adder_9_cout));
  Adder #(.width(1)) adder_10 (
    .a(multiplexer_1_out[1]), .b(multiplexer_2_out[0]), .out(out_6[1]), .cout(adder_10_cout));  // open: cin
  CSA4 csa4_1 (
    .inX({2'b00, multiplexer_1_out[3:2]}), .inY({1'b0, multiplexer_2_out[3:1]}), .Cin(multiplexer_4_out),
    .Cout(csa4_1_cout), .Result(csa4_1_result));
  Adder #(.width(4)) adder_11 (
    .a({1'b0, multiplexer_3_out}), .b(multiplexer_5_out), .out({adder_11_out, out_4[1]}),
    .cout(adder_11_cout[3]));  // open: cin
  Multiplexer #(.width(4)) multiplexer_6 (.in0(4'b0000), .in1(inX), .out(multiplexer_6_out), .sel(inY[2]));
  Adder #(.width(4)) adder_12 (
    .a({adder_11_cout[3], adder_11_out}), .b(multiplexer_6_out), .out({adder_12_out, out_4[2]}),
    .cout(adder_12_cout[3]));  // open: cin
  and and_9 (and_9_out, inX[0], inY[2]);
  Adder #(.width(1)) adder_13 (.a(and_9_out), .b(adder_7_out), .out(out_5[2]), .cout(adder_13_cout));  // open: cin
  and and_10 (and_10_out, inX[1], inY[2]);
  Adder #(.width(1)) adder_14 (
    .a(and_10_out), .b(adder_8_out), .out(adder_14_out), .cin(adder_13_cout), .cout(adder_14_cout));
  and and_11 (and_11_out, inX[2], inY[2]);
  Adder #(.width(1)) adder_15 (
    .a(and_11_out), .b(adder_9_out), .out(adder_15_out), .cin(adder_14_cout), .cout(adder_15_cout));
  and and_12 (and_12_out, inX[3], inY[2]);
  Adder #(.width(1)) adder_16 (
    .a(and_12_out), .b(adder_9_cout), .out(adder_16_out), .cin(adder_15_cout), .cout(adder_16_cout));
  Multiplexer #(.width(4)) multiplexer_7 (.in0(4'b0000), .in1(inX), .out(multiplexer_7_out), .sel(inY[3]));
  Multiplexer #(.width(4)) multiplexer_8 (.in0(4'b0000), .in1(inX), .out(multiplexer_8_out), .sel(inY[3]));
  Adder #(.width(1)) adder_17 (
    .a(adder_10_cout), .b(csa4_1_result[0]), .out(out_6[2]), .cout(adder_17_cout[0]));  // open: cin
  CSA4 csa4_2 (
    .inX({1'b0, csa4_1_result[3:1]}), .inY(csa4_1_cout), .Cin(multiplexer_7_out), .Cout(csa4_2_cout),
    .Result(csa4_2_result));
  Adder #(.width(4)) adder_18 (
    .a({adder_12_cout[3], adder_12_out}), .b(multiplexer_8_out), .out(out_4[6:3]), .cout(out_4[7]));  // open: cin
  and and_13 (and_13_out, inX[0], inY[3]);
  Adder #(.width(1)) adder_19 (.a(and_13_out), .b(adder_14_out), .out(out_5[3]), .cout(adder_19_cout));  // open: cin
  and and_14 (and_14_out, inX[1], inY[3]);
  Adder #(.width(1)) adder_20 (
    .a(and_14_out), .b(adder_15_out), .out(out_5[4]), .cin(adder_19_cout), .cout(adder_20_cout));
  and and_15 (and_15_out, inX[2], inY[3]);
  Adder #(.width(1)) adder_21 (
    .a(and_15_out), .b(adder_16_out), .out(out_5[5]), .cin(adder_20_cout), .cout(adder_21_cout));
  and and_16 (and_16_out, inX[3], inY[3]);
  Adder #(.width(1)) adder_22 (.a(and_16_out), .b(adder_16_cout), .out(out_5[6]), .cin(adder_21_cout), .cout(out_5[7]));
  Adder #(.width(5)) adder_23 (
    .a({csa4_2_cout, adder_17_cout[0]}), .b({1'b0, csa4_2_result}), .out(out_6[7:3]));  // open: cin, cout
  t3c t3c_1 (.Tin(1'b0), .y0(inY[0]), .y1(inY[1]), .sel(t3c_1_sel), .Tout(t3c_1_tout));
  Multiplexer #(.select(2), .width(5)) multiplexer_9 (
    .in0({5{1'b0}}), .in1({1'b0, inX}), .in2({inX, 1'b0}), .in3(negX), .out(multiplexer_9_out),
    .sel(t3c_1_sel));
  Adder #(.width(5)) adder_24 (
    .a(multiplexer_9_out), .b({5{1'b0}}), .out({adder_24_out, out_3[1:0]}));  // open: cin, cout
  Multiplexer #(.select(2), .width(5)) multiplexer_10 (
    .in0({5{1'b0}}), .in1({1'b0, inX}), .in2({inX, 1'b0}), .in3(negX), .out(multiplexer_10_out),
    .sel(t3c_2_sel));
  t3c t3c_2 (.Tin(t3c_1_tout), .y0(inY[2]), .y1(inY[3]), .sel(t3c_2_sel), .Tout(t3c_2_tout));
  assign bit_extender_1_out = {{2{adder_24_out[4]}}, adder_24_out};  // Bit_Extender bit_extender_1
  Adder #(.width(5)) adder_25 (
    .a(bit_extender_1_out), .b(multiplexer_10_out), .out({adder_25_out, out_3[3:2]}));  // open: cin, cout
  Multiplexer #(.width(4)) multiplexer_11 (.in0(4'b0000), .in1(inX), .out(multiplexer_11_out), .sel(t3c_2_tout));
  assign bit_extender_2_out = {{1{adder_25_out[4]}}, adder_25_out};  // Bit_Extender bit_extender_2
  Adder #(.width(4)) adder_26 (.a(bit_extender_2_out), .b(multiplexer_11_out), .out(out_3[7:4]));  // open: cin, cout

  // Other names for the same wires on the sheet: X[3:0] = inX; x0 = inX[0]; x1 = inX[1]; x2 = inX[2]; x3 = inX[3];
  //   y0 = inY[0]; y1 = inY[1]; y2 = inY[2]; y3 = inY[3]

  // Notes on the sheet:
  //   CSA based
  //   Simplified
  //   CRA based
  //   Radix-2
endmodule

module t3c (
  input  Tin,
  input  y0,
  input  y1,
  output [1:0] sel,
  output Tout
);

  wire and_1_out, and_2_out, not_1_out, or_1_out, xor_2_out;

  xor xor_1 (sel[0], Tin, y0);
  not not_1 (not_1_out, sel[0]);
  xor xor_2 (xor_2_out, y0, y1);
  and and_1 (and_1_out, sel[0], y1);
  and and_2 (and_2_out, not_1_out, xor_2_out);
  or or_1 (or_1_out, y0, Tin);
  or or_2 (sel[1], and_1_out, and_2_out);
  and and_3 (Tout, y1, or_1_out);
endmodule
